# Fritzing sketch Sandbox (saved by Fritzing 0.9.6b)
breadboards: 1

parts:
  Raspberry_Pi_1 = Raspberry Pi 3 [part_number=RPI-3-V1.2]
  R1 = Resistor [tolerance=±5% power=0.25 resistance=220 package=THT]
  LED1 = LED - 5mm [color="Red (633nm)" current=0.030 package="5 mm [THT]"]
  R2 = Resistor [tolerance=±5% power=0.25 resistance=220 package=THT]
  LED2 = LED - 5mm [color="Green (555nm)" current=0.030 package="5 mm [THT]"]

nets:
  N1: Raspberry_Pi_1.GPIO13, R2.Pin_1
  N2: Raspberry_Pi_1.GPIO26, R1.Pin_0
  N3: Raspberry_Pi_1.GND, LED1.cathode, LED2.cathode
  N4: R1.Pin_1, LED1.anode
  N5: R2.Pin_0, LED2.anode
